# Fritzing sketch frogbot (saved by Fritzing 0.9.3b)

parts:
  Raspberry_Pi_1 = Raspberry Pi 3 [part_number=RPI-3-V1.2]
  Part1 = Motor Driver 1A Dual TB6612FNG
  M2 = DC Motor
  M3 = DC Motor
  VCC1 = Battery
  hc-sr1 = hc-sr04
  LM1 = RioRand LM2596
  R1 = 2KΩ Resistor [package="1206 [SMD]"]
  R2 = 1K Ω Resistor [package="1206 [SMD]"]
  LED1 = LED - 5mm [color="Red (633nm)" package="5 mm [THT]"]
  LED2 = LED - 5mm [color="Red (633nm)" package="5 mm [THT]"]
  R3 = Resistor [tolerance=±5% resistance=220 package=THT]  # not connected
  R4 = Resistor [tolerance=±5% resistance=220 package=THT]  # not connected

nets:
  N1: Raspberry_Pi_1.GPIO22, LED2.anode
  N2: Raspberry_Pi_1.GPIO5, Part1.AIN2
  N3: Raspberry_Pi_1.GPIO6, Part1.AIN1
  N4: Raspberry_Pi_1.GPIO13, Part1.PWMB
  N5: Raspberry_Pi_1.GPIO19, Part1.BIN1
  N6: Raspberry_Pi_1.GPIO26, Part1.BIN2
  GND: Raspberry_Pi_1.GND, Part1.GND, VCC1.-, hc-sr1.GND, LM1.Pin_1, LM1.Pin_3, R1.Pin_0
  N7: Raspberry_Pi_1.GPIO21, hc-sr1.Trig
  N8: Raspberry_Pi_1.GPIO20, R1.Pin_1, R2.Pin_0
  N9: Raspberry_Pi_1.GPIO16, Part1.STBY
  N10: Raspberry_Pi_1.GPIO12, Part1.PWMA
  N11: Raspberry_Pi_1.GPIO23, LED1.anode
  VCC: Raspberry_Pi_1.5V, Part1.VCC, hc-sr1.VCC, LM1.Pin_2
  N12: Part1.B01, M3.pin_1
  N13: Part1.B02, M3.pin_2
  N14: Part1.A02, M2.pin_1
  N15: Part1.A01, M2.pin_2
  N16: Part1.VM, VCC1.+, LM1.Pin_0

custom parts:
  2KΩ Resistor: A generic resistor
  1K Ω Resistor: A generic resistor
